# Fritzing sketch mainArduino (saved by Fritzing 0.9.3b)
breadboards: 1

parts:
  부품1 = Arduino Nano (Rev3.0) (ICSP)
  hc-sr1 = hc-sr04
  LED1 = RGB LED (com. anode, rbg) [package="5 mm [THT]"]
  부품2 = Bluetooth HC-05 Macho
  J1 = Piezo Speaker
  U1 = LIPO-110mAh [package=lipo-110]
  부품3 = Power Cell LiPo Charger/Booster
  S1 = Toggle Switch [package=THT]

nets:
  GND: 부품1.GND, LED1.green_cathode, 부품2.GND, J1.pin1, U1.-, 부품3.GND
  N1: 부품1.D2, 부품2.TXD
  N2: 부품1.D3, 부품2.RXD
  N3: 부품1.D8, LED1.common_anode
  N4: 부품1.D9, J1.pin2
  N5: 부품1.VIN, S1.L2
  5V: 부품1.5V, hc-sr1.Trig, LED1.red_cathode, 부품2.VCC
  N6: 부품1.A0, hc-sr1.Echo
  N7: U1.+, 부품3.5VIN, S1.COM

notes:
  mainArduino
  A0 - Sound sensor
  D2 - HC05 (TX)
  D3 - HC05 (RX)
  D8 - NeoPixel (LED)
  D9 - Buzzer
